# Fritzing sketch BLERCCar (saved by Fritzing 0.9.10b)
breadboards: 2

parts:
  MH-ET_LIVE_ESP32_DEVKIT1 = MH-ET LIVE ESP32 DEVKIT 38 pins
  LED1 = smd LED [color="Red (633nm)" current=0A package="0805 [SMD]"]
  R1 = Resistor [tolerance=±5% resistance=1000 package="0603 [SMD]"]
  JACK1 = 2.1mm Barrel Jack with Terminal Block
  U1 = DC-DC_CONVERTER [package=dc-dc_converter]
  Part2 = Arduino Motor Shield (Rev3)
  M1 = DC Motor [voltage_(max)=6V voltage_(min)=3V]
  M2 = DC Motor [voltage_(max)=6V voltage_(min)=3V]
  HC-SR04_Sensor_1 = HC-SR04 Ultrasonic Distance Sensor
  HC-SR04_Sensor_2 = HC-SR04 Ultrasonic Distance Sensor

nets:
  N1: MH-ET_LIVE_ESP32_DEVKIT1.3V3, MH-ET_LIVE_ESP32_DEVKIT1.IO14, U1.SENSE
  N2: MH-ET_LIVE_ESP32_DEVKIT1.SVP, HC-SR04_Sensor_1.TRIG
  N3: MH-ET_LIVE_ESP32_DEVKIT1.SVN, HC-SR04_Sensor_1.ECHO
  N4: MH-ET_LIVE_ESP32_DEVKIT1.IO34, HC-SR04_Sensor_2.TRIG
  N5: MH-ET_LIVE_ESP32_DEVKIT1.IO35, HC-SR04_Sensor_2.ECHO
  N6: MH-ET_LIVE_ESP32_DEVKIT1.IO12, MH-ET_LIVE_ESP32_DEVKIT1.CMD, U1.VOUT
  N7: MH-ET_LIVE_ESP32_DEVKIT1.GND#58, U1.GND1
  N8: MH-ET_LIVE_ESP32_DEVKIT1.IO13, U1.VIN
  N9: MH-ET_LIVE_ESP32_DEVKIT1.SD2, U1.ON_OFF
  N10: MH-ET_LIVE_ESP32_DEVKIT1.GND#64, LED1.cathode, R1.Pin_0
  N11: MH-ET_LIVE_ESP32_DEVKIT1.IO23, LED1.anode
  N12: MH-ET_LIVE_ESP32_DEVKIT1.IO17, Part2.D11_PWM/B
  N13: MH-ET_LIVE_ESP32_DEVKIT1.IO16, Part2.D8/BreakeB
  N14: MH-ET_LIVE_ESP32_DEVKIT1.IO4, Part2.D13/DirB
  N15: MH-ET_LIVE_ESP32_DEVKIT1.IO0, Part2.D9/BreakeA
  N16: MH-ET_LIVE_ESP32_DEVKIT1.IO2, Part2.D12/DirA
  N17: MH-ET_LIVE_ESP32_DEVKIT1.IO15, Part2.D3_PWM/A
  N18: JACK1.POS, U1.TRIM, Part2.GND
  GND: JACK1.NEG, U1.GND2, Part2.VMOT, HC-SR04_Sensor_1.GND, HC-SR04_Sensor_2.GND
  N19: Part2.B-, M1.pin_2
  N20: Part2.B+, M1.pin_1
  N21: Part2.A-, M2.pin_2
  N22: Part2.A+, M2.pin_1
  VCC: Part2.5V, HC-SR04_Sensor_1.VCC, HC-SR04_Sensor_2.VCC

notes:
  12V
  5V Out
  7.5 - 12V in
  7.5~12V to 3.3V
  FrontLeft distance sensor
  TrigPin - 36
  EchoPin - 39
  FrontRight distance sensor
  TrigPin - 34
  EchoPin - 35

custom parts:
  MH-ET LIVE ESP32 DEVKIT 38 pins: http://mh.nodebb.com/topic/2/mh-et-live-esp32-devkit
