# Fritzing sketch BLERCcar Sketch (saved by Fritzing 0.9.10b)
breadboards: 2

parts:
  U1 = ESP32-38PinWide [part_number=ESP32-38PinWide]
  Part1 = Arduino Motor Shield (Rev3)
  M1_Steering = DC Motor [voltage_(max)=6V voltage_(min)=3V]
  M2_-_DriveShaft = DC Motor [voltage_(max)=6V voltage_(min)=3V]
  LED1 = LED - 5mm [color="Red (633nm)" current=0.030 package="5 mm [THT]"]
  R1 = Resistor [tolerance=±5% resistance=1k package="2512 [SMD]"]

nets:
  N1: U1.GND, R1.Pin_1
  N2: U1.GPIO15, Part1.D3_PWM/A
  N3: U1.GPIO2, Part1.D12/DirA
  N4: U1.GPIO0, Part1.D9/BreakeA
  N5: U1.GPIO4, Part1.D8/BreakeB
  N6: U1.GPIO16, Part1.D13/DirB
  N7: U1.GPIO17, Part1.D11_PWM/B
  N8: U1.GPIO23, LED1.anode
  N9: Part1.B-, M1_Steering.pin_2
  N10: Part1.B+, M1_Steering.pin_1
  N11: Part1.A-, M2_-_DriveShaft.pin_2
  N12: Part1.A+, M2_-_DriveShaft.pin_1
  N13: LED1.cathode, R1.Pin_0

notes:
  12v Power supply

custom parts:
  ESP32-38PinWide: Generic 38-Pin ESP32 with wide format (only access to one side of pins on a breadboard) based on Stephen Lilley's HiLetgo ESP-WROOM-32 ESP32 ESP-32S Development Board.
